# Fritzing sketch basic (saved by Fritzing 0.8.3b)
breadboards: 1

parts:
  Part1 = Arduino Mega 2560 (Rev3)
  LED1 = LED - 5mm [color="Red (633nm)" package="5 mm [THT]"]
  R1 = Resistor [package="2010 [SMD]"]
  S1 = Pushbutton [package="[THT]"]

nets:
  N1: Part1.D9_PWM, S1.Pin_3, S1.Pin_4
  N2: Part1.GND, R1.Pin_0, S1.Pin_1, S1.Pin_2
  N3: Part1.D4_PWM, LED1.anode
  N4: LED1.cathode, R1.Pin_1

notes:
  Adafruit LCD (pins 1-10)
