# Fritzing sketch bluetooth (saved by Fritzing 0.8.3b)
breadboards: 1

parts:
  Part1 = Arduino Mega 2560 (Rev3)
  LED1 = LED - 5mm [color="Red (633nm)" package="5 mm [THT]"]
  R1 = Resistor [package="2010 [SMD]"]
  S1 = Pushbutton [package="[THT]"]
  Part2 = Arduino Uno (Rev3)

nets:
  N1: Part1.D15/RX3, Part2.D7
  N2: Part1.D14/TX3, Part2.D6_PWM
  N3: Part1.D9_PWM, S1.Pin_3, S1.Pin_4
  5V: Part1.5V, Part2.5V
  GND: Part1.GND, R1.Pin_0, S1.Pin_1, S1.Pin_2, Part2.GND
  N4: Part1.D4_PWM, LED1.anode
  N5: LED1.cathode, R1.Pin_1

notes:
  RedBearLab BLE Shield should be attached
  Adafruit LCD (pins 1-10)
